# Fritzing sketch ICT-0217 (saved by Fritzing 0.9.3b)
breadboards: 1

parts:
  부품1 = Arduino Uno (Rev3)
  부품2 = Bluetooth HC-06
  R1 = Resistor [tolerance=±5% resistance=330 package=THT]
  R2 = Resistor [tolerance=±5% resistance=330 package=THT]
  R3 = Resistor [tolerance=±5% resistance=330 package=THT]
  부품3 = SRF05 Ultrasonic Rangefinder

nets:
  N1: 부품1.D12/MISO, 부품3.Echo
  GND: 부품1.GND, 부품2.GND, R3.Pin_0, 부품3.GND
  N2: 부품1.D2, 부품2.TXD
  N3: 부품1.D3_PWM, R1.Pin_1, R2.Pin_0
  VCC: 부품1.5V, 부품2.VCC, 부품3.VCC
  N4: 부품2.RXD, R1.Pin_0
  N5: R2.Pin_1, R3.Pin_1
